// Logisim project demultiplexer.circ as structural Verilog: 1 circuit, main circuit main
module main (
  input  Input,
  input  [2:0] Select_Line_Bits,
  output X0,
  output X1,
  output X2,
  output X3,
  output X4,
  output X6,
  output X7,
  output X5
);

  Demultiplexer #(.select(3)) demultiplexer_1 (
    .out0(X0), .out1(X1), .out2(X2), .out3(X3), .out4(X4), .out5(X5), .out6(X6), .out7(X7), .in(Input),
    .sel(Select_Line_Bits));  // open: en
endmodule
