// Logisim project multiplexer.circ as structural Verilog: 1 circuit, main circuit main
module main (
  input  D2,
  input  D1,
  input  D0,
  input  D3,
  input  D7,
  input  D6,
  input  D5,
  input  D4,
  input  [2:0] in_9
);

  wire multiplexer_1_out;

  Multiplexer #(.select(3)) multiplexer_1 (
    .in0(D0), .in1(D1), .in2(D2), .in3(D3), .in4(D4), .in5(D5), .in6(D6), .in7(D7), .out(multiplexer_1_out),
    .sel(in_9));  // open: en
  LED led_1 (.in(multiplexer_1_out));
endmodule
